# Fritzing sketch MegaPerfBoard3-updated (saved by Fritzing 0.9.2b)
circuit board: 8.49139cm x 5.37398cm
perfboards: 2
stripboards: 1

parts:
  J56 = female pin header, 4 pins [form="♀ (female)"]
  R1 = Resistor [tolerance=±5% resistance=10k package=THT]
  R2 = Resistor [tolerance=±5% resistance=10k package=THT]
  J57 = female pin header, 4 pins [form="♀ (female)"]
  J58 = female pin header, 4 pins [form="♀ (female)"]
  J59 = female pin header, 4 pins [form="♀ (female)"]
  J61 = female pin header, 2 pins [form="♀ (female)"]  # not connected
  J62 = female pin header, 2 pins [form="♀ (female)"]  # not connected
  R7 = Resistor [tolerance=±5% resistance=10k package=THT]
  R8 = Resistor [tolerance=±5% resistance=10k package=THT]
  J63 = female pin header, 1 pin [form="♀ (female)" part_number="Seatalk yellow"]
  J64 = female pin header, 1 pin [form="♀ (female)" part_number="Seatalk grey"]
  J65 = female pin header, 1 pin [form="♀ (female)" part_number="Seatalk red"]
  J66 = female pin header, 1 pin [form="♀ (female)" part_number="RS232 GND"]
  J67 = female pin header, 1 pin [form="♀ (female)" part_number="RS232 TX"]
  J68 = female pin header, 1 pin [form="♀ (female)" part_number="RS232 RX"]
  R9 = Resistor [tolerance=±5% resistance=3.9k package=THT]
  R10 = Resistor [tolerance=±5% resistance=6.8k package=THT]
  R11 = Resistor [tolerance=±5% resistance=2.2k package=THT]
  J53 = longpad pin header, 6 pins [form="long pad"]
  J46 = male pin header, 8 pins [form="♂ (male)"]
  J48 = male pin header, 8 pins [form="♂ (male)"]
  J60 = male pin header, 2 pins [form="♂ (male)"]
  J55 = female pin header, 10 pins [form="♀ (female)"]
  J54 = female pin header, 10 pins [form="♀ (female)"]
  part = female pin header, 10 pins [form="♀ (female)"]  # not connected
  Q4 = NPN-Transistor [package="TO92 [THT]"]
  Q3 = PNP-Transistor [package="TO92 [THT]"]
  U4 = Arduino Mega 2560 (Rev3)  # not connected

nets:
  N1: J56.pin1, R2.Pin_1, J46.pin5
  N2: J56.pin2, R1.Pin_1, J46.pin6
  N3: J56.pin3, J56.pin4, J57.pin2, J53.pin3, J55.pin5, J54.pin5
  N4: R1.Pin_0, R2.Pin_0, J57.pin1, J64.pin1, J66.pin1, R9.Pin_1, R10.Pin_1, J53.pin5, J55.pin6, J54.pin6, Q4.E
  N5: J57.pin3, J48.pin5
  N6: J57.pin4, J48.pin6
  N7: J58.pin1, J54.pin1
  N8: J58.pin2, J54.pin3
  N9: J58.pin3, J54.pin2
  N10: J58.pin4, J54.pin4
  N11: J59.pin1, J55.pin1
  N12: J59.pin2, J55.pin3
  N13: J59.pin3, J55.pin2
  N14: J59.pin4, J55.pin4
  N15: R7.Pin_0, J67.pin1
  N16: R7.Pin_1, R9.Pin_0, Q4.B
  N17: R8.Pin_0, R11.Pin_1, Q3.B
  N18: R8.Pin_1, J63.pin1, Q4.C
  N19: J65.pin1, R11.Pin_0, Q3.E
  N20: J68.pin1, R10.Pin_0, Q3.C
  N21: J48.pin1, J54.pin7
  N22: J48.pin2, J54.pin9
  N23: J48.pin3, J54.pin8
  N24: J48.pin4, J54.pin10
  N25: J60.pin1, J55.pin10
  N26: J60.pin2, J55.pin8

notes:
  Wind (Peet Bros)
  GPS
  GND
  5V
  TX
  RX
  NMEA
  TX3
  RX3
  TX2
  RX2
  TalkerTX
  TalkerRX
  TX (unused)
  RX (unused)
  Alarm output
  pins (40ma)
  Seatalk
  RS232
  RX (Blue)
  TX (White)
  GND(Green)
  Seatalk
  Grey (Gnd)
  Red (+ve)
  Yellow (Data)
  Seatalk (optional)
