# Fritzing sketch Seatalk (saved by Fritzing 0.9.2b)
circuit board: 4.31523cm x 1.99244cm
stripboards: 1

parts:
  R1 = Resistor [tolerance=±5% resistance=10k package=THT]
  J1 = female pin header, 1 pin [form="♀ (female)" part_number="Seatalk yellow"]
  J3 = female pin header, 1 pin [form="♀ (female)" part_number="Seatalk grey"]
  J5 = female pin header, 1 pin [form="♀ (female)" part_number="RS232 TX"]
  J6 = female pin header, 1 pin [form="♀ (female)" part_number="RS232 GND"]
  R3 = Resistor [tolerance=±5% resistance=10k package=THT]
  R4 = Resistor [tolerance=±5% resistance=6.8k package=THT]
  R5 = Resistor [tolerance=±5% resistance=2.2k package=THT]
  R6 = Resistor [tolerance=±5% resistance=3.9k package=THT]
  J4 = female pin header, 1 pin [form="♀ (female)" part_number="RS232 RX"]
  part = Resistor [tolerance=±5% resistance=220 package=THT]  # not connected
  Q2 = PNP-Transistor [package="TO92 [THT]"]
  Q1 = NPN-Transistor [package="TO92 [THT]"]
  J2 = female pin header, 1 pin [form="♀ (female)" part_number="Seatalk red"]

nets:
  N1: R1.Pin_0, R5.Pin_1, Q2.B
  N2: R1.Pin_1, J1.pin1, Q1.C
  N3: J3.pin1, J6.pin1, R4.Pin_1, R6.Pin_1, Q1.E
  N4: J5.pin1, R3.Pin_0
  N5: R3.Pin_1, R6.Pin_0, Q1.B
  N6: R4.Pin_0, J4.pin1, Q2.C
  N7: R5.Pin_0, Q2.E, J2.pin1

notes:
  Seatalk Side
  Grey (Gnd)
  Red (+ve)
  Yellow (Data)
  RS232 side
  RX (Blue)
  TX (White)
  GND(Green)
  RS232 to Seatalk
  Data
  GND
  12V+
  TX
  RX
  Based on information from Thomas Knauf http://www.thomasknauf.de/rap/seatalk1.htm#Har
