# Fritzing sketch Seatalk_modifier (saved by Fritzing 0.9.2b)
circuit board: 8.46667cm x 5.64444cm
breadboards: 1

parts:
  Q1 = NPN-Transistor [part_number=2N3904 package="TO92 [THT]"]
  Q2 = NPN-Transistor [part_number=C945 package="TO92 [THT]"]
  JP1 = Header 1 [part_number=GND package=1x01_offset]
  JP2 = Header 1 [part_number=TX package=1x01_offset]
  JP3 = Header 1 [part_number=RX package=1x01_offset]
  JP4 = Header 1 [part_number=Seatalk(Jaune) package=1x01_offset]
  JP5 = Header 1 [part_number=12V(Rouge) package=1x01_offset]
  JP6 = Header 1 [part_number=GND(Gris) package=1x01_offset]
  R1 = Resistor [tolerance=±5% resistance=220 package=THT]
  R2 = Resistor [tolerance=±5% resistance=10k package=THT]
  R3 = Resistor [tolerance=±5% resistance=10k package=THT]
  R4 = Resistor [tolerance=±5% resistance=10k package=THT]
  R5 = Resistor [tolerance=±5% resistance=3.9k package=THT]
  R6 = Resistor [tolerance=±5% resistance=10k package=THT]
  R7 = Resistor [tolerance=±5% resistance=2.2k package=THT]
  Q3 = PNP-Transistor [part_number=2N3906 package="TO92 [THT]"]
  R8 = Resistor [tolerance=±5% resistance=6.8k package=THT]
  Q4 = NPN-Transistor [package="TO92 [THT]"]
  R9 = Resistor [tolerance=±5% resistance=10k package=THT]
  R10 = Resistor [tolerance=±5% resistance=10k package=THT]
  R11 = Resistor [tolerance=±5% resistance=1k package=THT]
  R12 = Resistor [tolerance=±5% resistance=1k package=THT]

nets:
  N1: Q1.E, Q2.E, JP1.1, JP6.1, R2.Pin_1, R5.Pin_0, R8.Pin_1, Q4.E, R10.Pin_0, R11.Pin_0
  N2: Q1.B, R1.Pin_0
  N3: Q1.C, R2.Pin_0, R3.Pin_1, R4.Pin_1
  N4: Q2.B, R4.Pin_0, R5.Pin_1
  N5: Q2.C, JP4.1, R6.Pin_0
  N6: JP2.1, R1.Pin_1
  N7: JP3.1, Q4.C, R9.Pin_0, R10.Pin_1
  N8: JP5.1, R3.Pin_0, R7.Pin_1, Q3.E, R9.Pin_1
  N9: R6.Pin_1, R7.Pin_0, Q3.B
  N10: Q3.C, R8.Pin_0, R12.Pin_1
  N11: Q4.B, R11.Pin_1, R12.Pin_0
